# Fritzing sketch Schematics (saved by Fritzing 0.9.3b)

parts:
  Arduino_Uno = Arduino Uno (Rev3) - ICSP
  Arduino_Nano = Arduino Nano (Rev3.0)
  4X10W_white_LEDS = LEDs [package=led-1206]
  DC_12V_(_>_4A) = Power plug
  Q1 = npn-Powertransistor [package="TO220 [THT]"]
  3 = LEDs [package=led-1206]  # not connected
  2 = LEDs [package=led-1206]  # not connected
  1 = LEDs [package=led-1206]  # not connected

nets:
  GND: Arduino_Uno.GND, DC_12V_(_>_4A).GND
  N1: Arduino_Uno.D0/RX, Arduino_Nano.D1/TX
  N2: Arduino_Uno.D1/TX, Arduino_Nano.D0/RX
  VIN: Arduino_Uno.VIN, DC_12V_(_>_4A).VCC
  N3: Arduino_Nano.D9, Q1.collector
  N4: 4X10W_white_LEDS.C, Q1.emitter
